// Logisim project cao cpu simulation.circ as structural Verilog: 15 circuits, main circuit main
module main (
  input  in_1
);

  wire and_1_out, and_2_out, and_3_out, and_4_out, bit_extender_2_out, bit_extender_3_out, button_1_out,
       button_2_out, button_3_out, button_4_out, button_5_out, button_6_out, button_7_out, button_8_out,
       button_9_out, clock_1_out, decoder_1_out7, decoder_1_out8, decoder_1_out9, decoder_1_out10,
       decoder_1_out11, decoder_1_out12, decoder_1_out13, decoder_1_out14, decoder_1_out15, DR_ko_lagi_out,
       nor_1_out, not_1_out, not_2_out, or_1_out, or_2_out, or_3_out, or_4_out, or_5_out, or_6_out, or_7_out,
       or_9_out, or_10_out, or_11_out, undriven;
  wire [1:0] priority_encoder_2_out, priority_encoder_3_out, priority_encoder_4_out;
  wire [2:0] decoder_1_out4, or_8_out, priority_encoder_1_out;
  wire [3:0] decoder_1_out0, or_12_out;
  wire [14:0] AR_data_out, bit_extender_1_out, PC_data_out;
  wire [15:0] sc_1_t;
  wire [19:0] AC_data_out, alu_1_y, bit_extender_4_out, bit_extender_5_out, DR_data_out, IR_data_out,
       multiplexer_1_out, multiplexer_2_out, ram_1_data, TR_data_out;

  SC sc_1 (.T(sc_1_t));  // open: D_opcode_data_used_to_reset_clock_pulse, I, AR
  nor nor_1 (nor_1_out, sc_1_t[0], sc_1_t[1]);
  Decoder #(.select(4)) decoder_1 (
    .out0(decoder_1_out0[0]), .out1(decoder_1_out0[1]), .out2(decoder_1_out0[2]), .out3(decoder_1_out0[3]),
    .out4(decoder_1_out4[0]), .out5(decoder_1_out4[1]), .out6(decoder_1_out4[2]), .out7(decoder_1_out7),
    .out8(decoder_1_out8), .out9(decoder_1_out9), .out10(decoder_1_out10), .out11(decoder_1_out11),
    .out12(decoder_1_out12), .out13(decoder_1_out13), .out14(decoder_1_out14), .out15(decoder_1_out15),
    .sel(IR_data_out[18:15]), .en(nor_1_out));
  or or_1 (or_1_out, and_1_out, in_1);
  buf or_2 (or_2_out, and_2_out);  // OR_Gate
  and and_1 (and_1_out, sc_1_t[5], decoder_1_out9);
  buf or_3 (or_3_out, sc_1_t[0]);  // OR_Gate
  or or_4 (or_4_out, sc_1_t[1], and_3_out);
  buf or_5 (or_5_out, sc_1_t[2]);  // OR_Gate
  and and_2 (and_2_out, sc_1_t[4], decoder_1_out9);
  or DR_ko_lagi (DR_ko_lagi_out, decoder_1_out0[0], decoder_1_out0[1], decoder_1_out0[2], decoder_1_out0[3], decoder_1_out4[0], decoder_1_out4[1], decoder_1_out4[2], decoder_1_out7, decoder_1_out11, decoder_1_out12);
  or or_6 (or_6_out, sc_1_t[2], sc_1_t[0]);
  and and_3 (and_3_out, sc_1_t[4], DR_ko_lagi_out);
  Priority_Encoder priority_encoder_1 (
    .in1(or_2_out), .in2(or_3_out), .in5(or_5_out), .in7(or_4_out), .out(priority_encoder_1_out), .en_in(1'b1));  // open: in0, in3, in4, in6, gs, en_out
  or or_7 (or_7_out, and_3_out, sc_1_t[1]);
  // Probe on multiplexer_2_out
  Bit_Extender #(.in_width(20), .out_width(15)) bit_extender_1 (.in(multiplexer_2_out), .out(bit_extender_1_out));
  and and_4 (and_4_out, decoder_1_out0[0], sc_1_t[5]);
  // Probe on bit_extender_1_out
  assign or_8_out = decoder_1_out4;  // OR_Gate or_8, 3 bits wide OR_Gate
  Button button_1 (.out(button_1_out));
  Bit_Extender #(.in_width(3), .out_width(1)) bit_extender_2 (.in(or_8_out), .out(bit_extender_2_out));
  or or_9 (or_9_out, decoder_1_out0[0], decoder_1_out4[0]);
  buf or_10 (or_10_out, decoder_1_out4[2]);  // OR_Gate
  buf or_11 (or_11_out, decoder_1_out4[2]);  // OR_Gate
  // Probe on priority_encoder_1_out
  Button button_2 (.out(button_2_out));
  assign or_12_out = decoder_1_out0;  // OR_Gate or_12, 4 bits wide OR_Gate
  not not_1 (not_1_out, or_11_out);
  _15Bit_Custom_Register AR (
    .Data_In(bit_extender_1_out), .Data_Out(AR_data_out), .CLR(button_2_out), .INC(button_1_out),
    .LDA(or_6_out));
  Bit_Extender #(.in_width(4), .out_width(1)) bit_extender_3 (.in(or_12_out), .out(bit_extender_3_out));
  not not_2 (not_2_out, decoder_1_out4[1]);
  Priority_Encoder #(.select(2)) priority_encoder_2 (
    .in0(bit_extender_2_out), .in1(bit_extender_3_out), .out(priority_encoder_2_out));  // open: in2, in3, gs, en_out, en_in
  Priority_Encoder #(.select(2)) priority_encoder_3 (
    .in0(or_9_out), .in1(decoder_1_out4[1]), .in2(or_10_out), .out(priority_encoder_3_out));  // open: in3, gs, en_out, en_in
  Priority_Encoder #(.select(2)) priority_encoder_4 (
    .in1(or_11_out), .in3(not_1_out), .out(priority_encoder_4_out));  // open: in0, in2, gs, en_out, en_in
  Multiplexer #(.select(2), .width(20)) multiplexer_1 (
    .in1(multiplexer_2_out), .in3(AC_data_out), .out(multiplexer_1_out), .sel(priority_encoder_4_out));  // open: in0, in2, en
  Button button_3 (.out(button_3_out));
  Button button_4 (.out(button_4_out));
  Button button_5 (.out(button_5_out));
  Button button_6 (.out(button_6_out));
  _20Bit_Custom_Register IR (
    .Data_In(multiplexer_2_out), .Data_Out(IR_data_out), .CLR(button_7_out), .INC(button_3_out),
    .LDA(sc_1_t[1]));
  Button button_7 (.out(button_7_out));
  Button button_8 (.out(button_8_out));
  _15Bit_Custom_Register PC (
    .Data_In(bit_extender_1_out), .Data_Out(PC_data_out), .CLR(button_4_out), .INC(sc_1_t[1]), .LDA(and_2_out));
  _20Bit_Custom_Register DR (
    .Data_In(multiplexer_2_out), .Data_Out(DR_data_out), .CLR(button_6_out), .INC(button_5_out),
    .LDA(and_3_out));
  // Probe on IR_data_out
  _20Bit_Custom_Register TR (
    .Data_In(multiplexer_2_out), .Data_Out(TR_data_out), .CLR(button_9_out), .INC(button_8_out));  // open: LDA
  Button button_9 (.out(button_9_out));
  // Probe on AR_data_out
  // Probe on PC_data_out
  ALU alu_1 (
    .A(multiplexer_1_out), .B(DR_data_out), .Y(alu_1_y), .Cin(not_2_out), .S0_S1(priority_encoder_3_out),
    .S2_S3(priority_encoder_2_out));  // open: out_6
  _20Bit_Custom_Register AC (.Data_In(alu_1_y), .Data_Out(AC_data_out), .LDA(undriven));  // open: CLR, INC
  assign bit_extender_4_out = {{5{1'b0}}, AR_data_out};  // Bit_Extender bit_extender_4
  assign bit_extender_5_out = {{5{1'b0}}, PC_data_out};  // Bit_Extender bit_extender_5
  // Probe on DR_data_out
  Clock clock_1 (.out(clock_1_out));
  // Probe on bit_extender_5_out
  RAM #(.addrWidth(15), .dataWidth(20)) ram_1 (
    .addr(AR_data_out), .data(ram_1_data), .sel(or_7_out), .clk(clock_1_out), .ld(or_7_out));  // open: clr
  // Probe on ram_1_data
  Multiplexer #(.select(3), .width(20)) multiplexer_2 (
    .in1(bit_extender_4_out), .in2(bit_extender_5_out), .in3(DR_data_out), .in4(AC_data_out),
    .in5(IR_data_out), .in6(TR_data_out), .in7(ram_1_data), .out(multiplexer_2_out),
    .sel(priority_encoder_1_out), .en(1'b1));  // open: in0

  // Notes on the sheet:
  //   T
  //   T4
  //   BUN
  //   BUN
  //   BUN
  //   DR ma memoy load garna
  //   t5
  //   and
  //   LDA
  //   if 0-5: logic
  //   s2,s3
  //   s0,s1
  //   Cin
  //   20 Bit Data Bus
  //   2
  //   3
  //   4
  //   5
  //   6
  //   7
  //   1
endmodule

module SC (
  input  [3:0] D_opcode_data_used_to_reset_clock_pulse,
  input  [14:0] AR,
  input  I,
  output [15:0] T
);

  wire and_1_out, and_2_out, and_3_out, and_4_out, button_1_out, clock_1_out, clock_2_out, d_ff_1_q,
       decoder_2_out0, decoder_2_out1, decoder_2_out2, decoder_2_out3, decoder_2_out4, decoder_2_out5,
       decoder_2_out6, decoder_2_out7, decoder_2_out8, decoder_2_out9, decoder_2_out10, decoder_2_out11,
       decoder_2_out12, decoder_2_out13, decoder_2_out14, decoder_2_out15, not_1_out, not_2_out, not_3_out,
       or_1_out, or_2_out, or_3_out, or_4_out, or_5_out;
  wire [3:0] counter_1_q, undriven;

  not not_1 (not_1_out, I);
  or or_1 (or_1_out, T[0], T[3]);
  Clock clock_1 (.out(clock_1_out));
  not not_2 (not_2_out, and_1_out);
  and and_1 (and_1_out, decoder_2_out15, or_1_out, AR[0], not_1_out);
  D_Flip_Flop d_ff_1 (.clk(clock_1_out), .D(not_2_out), .Q(d_ff_1_q), .en(or_2_out));  // open: Qn, preset, reset
  or or_2 (or_2_out, and_1_out, T[0]);
  Counter #(.width(4), .max('hf)) counter_1 (
    .D(undriven), .count(d_ff_1_q), .Q(counter_1_q), .clk(clock_2_out), .clr(or_3_out));  // open: load, carry
  Clock clock_2 (.out(clock_2_out));
  Decoder #(.select(4), .disabled(0)) decoder_1 (
    .out0(T[0]), .out1(T[1]), .out2(T[2]), .out3(T[3]), .out4(T[4]), .out5(T[5]), .out6(T[6]), .out7(T[7]),
    .out8(T[8]), .out9(T[9]), .out10(T[10]), .out11(T[11]), .out12(T[12]), .out13(T[13]), .out14(T[14]),
    .out15(T[15]), .sel(counter_1_q));  // open: en
  not not_3 (not_3_out, d_ff_1_q);
  or or_3 (or_3_out, and_3_out, and_2_out, not_3_out, and_4_out, button_1_out);
  Button button_1 (.out(button_1_out));
  and and_2 (and_2_out, T[6], or_4_out);
  or or_4 (or_4_out, decoder_2_out6, decoder_2_out0, decoder_2_out1, decoder_2_out2, decoder_2_out3, decoder_2_out4, decoder_2_out5, decoder_2_out9);
  and and_3 (and_3_out, T[5], or_5_out);
  or or_5 (or_5_out, decoder_2_out7, decoder_2_out8);
  and and_4 (and_4_out, T[7], decoder_2_out10);
  Decoder #(.select(4)) decoder_2 (
    .out0(decoder_2_out0), .out1(decoder_2_out1), .out2(decoder_2_out2), .out3(decoder_2_out3),
    .out4(decoder_2_out4), .out5(decoder_2_out5), .out6(decoder_2_out6), .out7(decoder_2_out7),
    .out8(decoder_2_out8), .out9(decoder_2_out9), .out10(decoder_2_out10), .out11(decoder_2_out11),
    .out12(decoder_2_out12), .out13(decoder_2_out13), .out14(decoder_2_out14), .out15(decoder_2_out15),
    .sel(D_opcode_data_used_to_reset_clock_pulse));  // open: en

  // Notes on the sheet:
  //   T5
  //   7
  //   8
endmodule

module ALU (
  input  Cin,
  input  [19:0] A,
  input  [19:0] B,
  input  [1:0] S2_S3,
  input  [1:0] S0_S1,
  output out_6,
  output [19:0] Y
);

  wire [19:0] arithmetic_cicuit_1_sout, logical_circuit_1_yout;

  Arithmetic_Cicuit arithmetic_cicuit_1 (
    .Cin(Cin), .A(A), .B(B), .S0_S1(S0_S1), .Sout(arithmetic_cicuit_1_sout), .out_6(out_6));
  Logical_Circuit logical_circuit_1 (.Yout(logical_circuit_1_yout), .S0_S1(S0_S1), .A(A), .B(B));
  Multiplexer #(.select(2), .width(20)) multiplexer_1 (
    .in0(arithmetic_cicuit_1_sout), .in1(logical_circuit_1_yout), .out(Y), .sel(S2_S3), .en(1'b1));  // open: in2, in3
endmodule

module Arithmetic_Cicuit (
  input  Cin,
  input  [19:0] A,
  input  [19:0] B,
  input  [1:0] S0_S1,
  output [19:0] Sout,
  output out_6
);

  wire [19:0] bit_extender_1_out, multiplexer_1_out, not_1_out, not_2_out;

  assign bit_extender_1_out = {{19{1'b0}}, 1'b0};  // Bit_Extender bit_extender_1
  assign not_1_out = ~B;  // NOT_Gate not_1, 20 bits wide
  assign not_2_out = ~bit_extender_1_out;  // NOT_Gate not_2, 20 bits wide
  Multiplexer #(.select(2), .width(20)) multiplexer_1 (
    .in0(B), .in1(not_1_out), .in2(bit_extender_1_out), .in3(not_2_out), .out(multiplexer_1_out),
    .sel(S0_S1), .en(1'b1));
  Adder #(.width(20)) adder_1 (.a(A), .b(multiplexer_1_out), .out(Sout), .cin(Cin), .cout(out_6));
  // Probe on out_6
endmodule

module Logical_Circuit (
  input  [19:0] A,
  input  [19:0] B,
  input  [1:0] S0_S1,
  output [19:0] Yout
);

  wire [19:0] and_2_out, not_1_out, or_2_out, xor_1_out;

  // Probe on and_2_out
  assign and_2_out = A & B;  // AND_Gate and_2, 20 bits wide
  // Probe on or_2_out
  assign or_2_out = A | B;  // OR_Gate or_2, 20 bits wide
  assign xor_1_out = A ^ B;  // XOR_Gate xor_1, 20 bits wide
  assign not_1_out = ~A;  // NOT_Gate not_1, 20 bits wide
  // Probe on xor_1_out
  // Probe on not_1_out
  Multiplexer #(.select(2), .width(20)) multiplexer_1 (
    .in0(and_2_out), .in1(or_2_out), .in2(xor_1_out), .in3(not_1_out), .out(Yout), .sel(S0_S1));  // open: en
endmodule

module CPU_BUS (
);

  wire button_1_out, button_2_out, button_3_out, button_4_out, button_5_out, button_6_out, button_7_out,
       clock_1_out, or_4_out;
  wire [2:0] or_1_out;
  wire [14:0] AR_data_out, bit_extender_1_out, PC_data_out;
  wire [15:0] sc_1_t;
  wire [19:0] AC_data_out, bit_extender_2_out, bit_extender_3_out, DR_data_out, IR_data_out,
       multiplexer_1_out, ram_1_data, TR_data_out;

  SC sc_1 (.T(sc_1_t));  // open: D_opcode_data_used_to_reset_clock_pulse, I, AR
  or or_1 (or_1_out[0], sc_1_t[1], 1'b0);
  or or_2 (or_1_out[1], sc_1_t[0], sc_1_t[1], 1'b0);
  or or_3 (or_1_out[2], sc_1_t[1], 1'b0);
  buf or_4 (or_4_out, sc_1_t[0]);  // OR_Gate
  // Probe on multiplexer_1_out
  Bit_Extender #(.in_width(20), .out_width(15)) bit_extender_1 (.in(multiplexer_1_out), .out(bit_extender_1_out));
  // Probe on bit_extender_1_out
  Button button_1 (.out(button_1_out));
  Button button_2 (.out(button_2_out));
  _15Bit_Custom_Register AR (
    .Data_In(bit_extender_1_out), .Data_Out(AR_data_out), .CLR(button_2_out), .INC(button_1_out),
    .LDA(or_4_out));
  // Probe on or_1_out
  Button button_3 (.out(button_3_out));
  Button button_4 (.out(button_4_out));
  ALU alu_1 ();  // open: A, B, Y, Cin, S0_S1, S2_S3, out_6
  _20Bit_Custom_Register IR (
    .Data_In(multiplexer_1_out), .Data_Out(IR_data_out), .CLR(button_5_out), .INC(button_3_out),
    .LDA(sc_1_t[1]));
  Button button_5 (.out(button_5_out));
  Button button_6 (.out(button_6_out));
  _15Bit_Custom_Register PC (
    .Data_In(bit_extender_1_out), .Data_Out(PC_data_out), .CLR(button_4_out), .INC(sc_1_t[1]), .LDA(1'b0));
  _20Bit_Custom_Register DR (.Data_In(multiplexer_1_out), .Data_Out(DR_data_out));  // open: CLR, INC, LDA
  _20Bit_Custom_Register TR (
    .Data_In(multiplexer_1_out), .Data_Out(TR_data_out), .CLR(button_7_out), .INC(button_6_out));  // open: LDA
  Button button_7 (.out(button_7_out));
  // Probe on AR_data_out
  // Probe on PC_data_out
  // Probe on IR_data_out
  assign bit_extender_2_out = {{5{1'b0}}, AR_data_out};  // Bit_Extender bit_extender_2
  assign bit_extender_3_out = {{5{1'b0}}, PC_data_out};  // Bit_Extender bit_extender_3
  _20Bit_Custom_Register AC (.Data_Out(AC_data_out));  // open: Data_In, CLR, INC, LDA
  Clock clock_1 (.out(clock_1_out));
  // Probe on bit_extender_3_out
  RAM #(.addrWidth(15), .dataWidth(20)) ram_1 (
    .addr(AR_data_out), .data(ram_1_data), .sel(sc_1_t[1]), .clk(clock_1_out), .ld(sc_1_t[1]));  // open: clr
  // Probe on ram_1_data
  Multiplexer #(.select(3), .width(20)) multiplexer_1 (
    .in1(bit_extender_2_out), .in2(bit_extender_3_out), .in3(DR_data_out), .in4(AC_data_out),
    .in5(IR_data_out), .in6(TR_data_out), .in7(ram_1_data), .out(multiplexer_1_out), .sel(or_1_out), .en(1'b1));  // open: in0

  // Notes on the sheet:
  //   20 Bit Data Bus
  //   7
  //   1
endmodule

module _15Bit_Custom_Register (
  input  [14:0] Data_In,
  input  CLR,
  input  LDA,
  input  INC,
  output [14:0] Data_Out
);

  wire clock_1_out, or_1_out;
  wire [14:0] adder_1_out, bit_extender_1_out, multiplexer_1_out;

  Multiplexer #(.width(15)) multiplexer_1 (
    .in0(Data_In), .in1(adder_1_out), .out(multiplexer_1_out), .sel(INC), .en(1'b1));
  or or_1 (or_1_out, INC, CLR, LDA);
  Clock clock_1 (.out(clock_1_out));
  Register #(.width(15)) register_1 (.D(multiplexer_1_out), .en(or_1_out), .Q(Data_Out), .clk(clock_1_out), .clr(CLR));
  assign bit_extender_1_out = {{14{1'b0}}, 1'b1};  // Bit_Extender bit_extender_1
  Adder #(.width(15)) adder_1 (.a(Data_Out), .b(bit_extender_1_out), .out(adder_1_out), .cin(1'b0));  // open: cout

  // Notes on the sheet:
  //   15 bit custom register(Added Increment)
endmodule

module _20Bit_Custom_Register (
  input  [19:0] Data_In,
  input  CLR,
  input  INC,
  input  LDA,
  output [19:0] Data_Out
);

  wire CLK_out, or_1_out;
  wire [19:0] adder_1_out, bit_extender_1_out, multiplexer_1_out;

  Multiplexer #(.width(20)) multiplexer_1 (
    .in0(Data_In), .in1(adder_1_out), .out(multiplexer_1_out), .sel(INC), .en(1'b1));
  or or_1 (or_1_out, INC, CLR, LDA);
  Clock CLK (.out(CLK_out));
  Register #(.width(20)) register_1 (.D(multiplexer_1_out), .en(or_1_out), .Q(Data_Out), .clk(CLK_out), .clr(CLR));
  assign bit_extender_1_out = {{19{1'b0}}, 1'b1};  // Bit_Extender bit_extender_1
  Adder #(.width(20)) adder_1 (.a(Data_Out), .b(bit_extender_1_out), .out(adder_1_out));  // open: cin, cout

  // Notes on the sheet:
  //   20 bit custom register(Added Increment)
endmodule

module ALU_V2 (
  input  [3:0] in_1,
  input  [19:0] A,
  input  [19:0] B,
  input  Bit_In,
  output [19:0] out_5,
  output Bit_Out
);

  wire and_1_out, and_2_out, and_3_out, and_4_out, and_5_out, and_6_out, arithmetic_v2_1_out_5,
       multiplexer_2_out, nor_1_out, not_1_out, not_2_out, not_3_out, not_4_out, or_1_out, or_2_out;
  wire [1:0] priority_encoder_1_out;
  wire [19:0] arithmetic_v2_1_sout, logic_v2_1_yout, multiplexer_1_out, multiplexer_3_out;

  not not_1 (not_1_out, in_1[1]);
  not not_2 (not_2_out, in_1[0]);
  and and_1 (and_1_out, in_1[3], in_1[2], not_2_out, not_1_out);
  and and_2 (and_2_out, in_1[3], in_1[2], in_1[1], in_1[0]);
  and and_3 (and_3_out, in_1[3], not_3_out);
  and and_4 (and_4_out, in_1[3], in_1[2]);
  not not_3 (not_3_out, in_1[2]);
  nor nor_1 (nor_1_out, and_2_out, and_1_out);
  and and_5 (and_5_out, and_4_out, nor_1_out);
  // Probe on B
  Multiplexer #(.width(20)) multiplexer_1 (
    .in0({Bit_In, A[19:1]}), .in1({A[18:0], Bit_In}), .out(multiplexer_1_out), .sel(and_6_out));  // open: en
  or or_1 (or_1_out, and_3_out, and_5_out);
  Arithmetic_v2 arithmetic_v2_1 (
    .Sout(arithmetic_v2_1_sout), .A(A), .B(B), .out_5(arithmetic_v2_1_out_5),
    .S0_S1___00_add_01_sub_10_dec__11_inc(in_1[1:0]));
  Logic_v2 logic_v2_1 (.Yout(logic_v2_1_yout), .A(A), .B(B), .S0_S1(in_1[1:0]));
  Multiplexer multiplexer_2 (.in0(A[0]), .in1(A[19]), .out(multiplexer_2_out), .sel(and_6_out));  // open: en
  and and_6 (and_6_out, or_1_out, and_5_out);
  Multiplexer #(.width(20)) multiplexer_3 (
    .in0(arithmetic_v2_1_sout), .in1(logic_v2_1_yout), .out(multiplexer_3_out), .sel(in_1[2]));  // open: en
  // Probe on multiplexer_1_out
  Multiplexer multiplexer_4 (
    .in0(arithmetic_v2_1_out_5), .in1(multiplexer_2_out), .out(Bit_Out), .sel(or_1_out));  // open: en
  // Probe on multiplexer_3_out
  // Probe on out_5
  not not_4 (not_4_out, or_2_out);
  or or_2 (or_2_out, and_1_out, and_2_out, or_1_out);
  Multiplexer #(.select(2), .width(20)) multiplexer_5 (
    .in0(multiplexer_3_out), .in1(multiplexer_1_out), .in2(A), .in3(B), .out(out_5),
    .sel(priority_encoder_1_out));  // open: en
  Priority_Encoder #(.select(2)) priority_encoder_1 (
    .in0(not_4_out), .in1(or_1_out), .in2(and_2_out), .in3(and_1_out), .out(priority_encoder_1_out));

  // Notes on the sheet:
  //   11
  //   10
endmodule

module Arithmetic_v2 (
  input  [19:0] A,
  input  [19:0] B,
  input  [1:0] S0_S1___00_add_01_sub_10_dec__11_inc,
  output [19:0] Sout,
  output out_5
);

  wire and_1_out, and_2_out, or_1_out, xor_1_out;
  wire [19:0] multiplexer_1_out, not_1_out, not_2_out;

  assign not_1_out = ~B;  // NOT_Gate not_1, 20 bits wide
  assign not_2_out = ~{20{1'b0}};  // NOT_Gate not_2, 20 bits wide
  Multiplexer #(.select(2), .width(20)) multiplexer_1 (
    .in0(B), .in1(not_1_out), .in2(not_2_out), .in3({20{1'b0}}), .out(multiplexer_1_out),
    .sel(S0_S1___00_add_01_sub_10_dec__11_inc));  // open: en
  xor xor_1 (xor_1_out, S0_S1___00_add_01_sub_10_dec__11_inc[0], S0_S1___00_add_01_sub_10_dec__11_inc[1]);
  and and_1 (and_1_out, S0_S1___00_add_01_sub_10_dec__11_inc[1], S0_S1___00_add_01_sub_10_dec__11_inc[0]);
  and and_2 (and_2_out, xor_1_out, S0_S1___00_add_01_sub_10_dec__11_inc[0]);
  or or_1 (or_1_out, and_1_out, and_2_out);
  Adder #(.width(20)) adder_1 (.a(A), .b(multiplexer_1_out), .out(Sout), .cin(or_1_out), .cout(out_5));
endmodule

module Logic_v2 (
  input  [19:0] A,
  input  [19:0] B,
  input  [1:0] S0_S1,
  output [19:0] Yout
);

  wire [19:0] and_2_out, nand_1_out, not_1_out, or_2_out;

  // Probe on and_2_out
  assign and_2_out = A & B;  // AND_Gate and_2, 20 bits wide
  // Probe on or_2_out
  assign or_2_out = A | B;  // OR_Gate or_2, 20 bits wide
  assign nand_1_out = ~(A & B);  // NAND_Gate nand_1, 20 bits wide
  assign not_1_out = ~A;  // NOT_Gate not_1, 20 bits wide
  // Probe on nand_1_out
  // Probe on not_1_out
  Multiplexer #(.select(2), .width(20)) multiplexer_1 (
    .in0(and_2_out), .in1(or_2_out), .in2(nand_1_out), .in3(not_1_out), .out(Yout), .sel(S0_S1));  // open: en
endmodule

module Shift_circuit (
  input  [19:0] A,
  input  S_0_shift_right__1__shift_left,
  input  extra_bit_in,
  output [19:0] Aout,
  output extra_bit_out
);

  Multiplexer #(.width(20)) multiplexer_1 (
    .in0({extra_bit_in, A[19:1]}), .in1({A[18:0], extra_bit_in}), .out(Aout),
    .sel(S_0_shift_right__1__shift_left));  // open: en
  Multiplexer multiplexer_2 (
    .in0(A[0]), .in1(A[19]), .out(extra_bit_out), .sel(S_0_shift_right__1__shift_left));  // open: en
endmodule

module mainv2 (
);

  wire ac_1_out_6, and_1_out, and_2_out, and_3_out, and_4_out, and_5_out, and_6_out, BSA_t4_out, BSA_t5_out,
       button_1_out, button_2_out, button_3_out, button_4_out, button_5_out, button_6_out, button_7_out,
       clock_1_out, decoder_1_out0, decoder_1_out1, decoder_1_out2, decoder_1_out3, decoder_1_out4,
       decoder_1_out5, decoder_1_out6, decoder_1_out7, decoder_1_out8, decoder_1_out9, decoder_1_out10,
       decoder_1_out11, decoder_1_out12, decoder_1_out13, decoder_1_out14, decoder_1_out15, DR_ko_lagi_out,
       nor_1_out, not_1_out, or_1_out, or_2_out, or_3_out, or_4_out, or_5_out, or_6_out, or_7_out, or_8_out,
       or_9_out, or_10_out;
  wire [2:0] priority_encoder_1_out;
  wire [3:0] IR_data_out;
  wire [14:0] AR_data_out, bit_extender_1_out, PC_data_out;
  wire [15:0] sc_1_t;
  wire [19:0] ac_1_out_5, bit_extender_2_out, bit_extender_3_out, DR_data_out, IR_data_out_2,
       multiplexer_1_out, ram_1_data, TR_data_out;

  SC sc_1 (.T(sc_1_t), .D_opcode_data_used_to_reset_clock_pulse(IR_data_out), .I(IR_data_out_2[19]), .AR(AR_data_out));
  nor nor_1 (nor_1_out, sc_1_t[0], sc_1_t[1]);
  Decoder #(.select(4)) decoder_1 (
    .out0(decoder_1_out0), .out1(decoder_1_out1), .out2(decoder_1_out2), .out3(decoder_1_out3),
    .out4(decoder_1_out4), .out5(decoder_1_out5), .out6(decoder_1_out6), .out7(decoder_1_out7),
    .out8(decoder_1_out8), .out9(decoder_1_out9), .out10(decoder_1_out10), .out11(decoder_1_out11),
    .out12(decoder_1_out12), .out13(decoder_1_out13), .out14(decoder_1_out14), .out15(decoder_1_out15),
    .sel(IR_data_out), .en(nor_1_out));
  or or_1 (or_1_out, BSA_t5_out, and_4_out);
  and and_1 (and_1_out, sc_1_t[4], decoder_1_out7);
  and and_2 (and_2_out, sc_1_t[6], decoder_1_out10);
  or or_2 (or_2_out, BSA_t4_out, sc_1_t[0]);
  or or_3 (or_3_out, sc_1_t[1], and_3_out, and_5_out);
  not not_1 (not_1_out, decoder_1_out15);
  and BSA_t4 (BSA_t4_out, sc_1_t[4], decoder_1_out9);
  and BSA_t5 (BSA_t5_out, sc_1_t[5], decoder_1_out9);
  buf or_4 (or_4_out, sc_1_t[2]);  // OR_Gate
  and and_3 (and_3_out, sc_1_t[3], IR_data_out_2[19], not_1_out);
  and and_4 (and_4_out, sc_1_t[4], decoder_1_out8);
  or DR_ko_lagi (DR_ko_lagi_out, decoder_1_out0, decoder_1_out1, decoder_1_out2, decoder_1_out3, decoder_1_out4, decoder_1_out5, decoder_1_out6, decoder_1_out10, decoder_1_out11, decoder_1_out12);
  or or_5 (or_5_out, sc_1_t[2], and_3_out, sc_1_t[0]);
  and and_5 (and_5_out, sc_1_t[4], DR_ko_lagi_out);
  Priority_Encoder priority_encoder_1 (
    .in1(or_1_out), .in2(or_2_out), .in3(and_2_out), .in4(and_1_out), .in5(or_4_out), .in7(or_3_out),
    .out(priority_encoder_1_out), .en_in(1'b1));  // open: in0, in6, gs, en_out
  or or_6 (or_6_out, and_5_out, sc_1_t[1]);
  // Probe on multiplexer_1_out
  Bit_Extender #(.in_width(20), .out_width(15)) bit_extender_1 (.in(multiplexer_1_out), .out(bit_extender_1_out));
  // Probe on bit_extender_1_out
  and and_6 (and_6_out, sc_1_t[5], decoder_1_out10);
  // Probe on priority_encoder_1_out
  Button button_1 (.out(button_1_out));
  _15Bit_Custom_Register AR (
    .Data_In(bit_extender_1_out), .Data_Out(AR_data_out), .CLR(button_1_out), .INC(BSA_t4_out), .LDA(or_5_out));
  Button button_2 (.out(button_2_out));
  Button button_3 (.out(button_3_out));
  or or_7 (or_7_out, BSA_t5_out, and_4_out);
  Button button_4 (.out(button_4_out));
  _20Bit_Custom_Register IR (
    .Data_In(multiplexer_1_out), .Data_Out({IR_data_out_2[19], IR_data_out, IR_data_out_2[14:0]}),
    .CLR(button_5_out), .INC(button_2_out), .LDA(sc_1_t[1]));
  Button button_5 (.out(button_5_out));
  Button button_6 (.out(button_6_out));
  _15Bit_Custom_Register PC (
    .Data_In(bit_extender_1_out), .Data_Out(PC_data_out), .CLR(button_3_out), .INC(sc_1_t[1]), .LDA(or_7_out));
  _20Bit_Custom_Register DR (
    .Data_In(multiplexer_1_out), .Data_Out(DR_data_out), .CLR(button_4_out), .INC(and_6_out), .LDA(and_5_out));
  AC ac_1 (
    .D(DR_data_out), .Time_Input(sc_1_t), .D_2(IR_data_out), .out_5(ac_1_out_5), .out_6(ac_1_out_6),
    .Bus(multiplexer_1_out));
  // Probe on {IR_data_out_2[19], IR_data_out, IR_data_out_2[14:0]}
  _20Bit_Custom_Register TR (
    .Data_In(multiplexer_1_out), .Data_Out(TR_data_out), .CLR(button_7_out), .INC(button_6_out));  // open: LDA
  Button button_7 (.out(button_7_out));
  // Probe on AR_data_out
  // Probe on multiplexer_1_out
  or or_8 (or_8_out, and_2_out, or_6_out, and_3_out, and_3_out);
  // Probe on PC_data_out
  assign bit_extender_2_out = {{5{1'b0}}, AR_data_out};  // Bit_Extender bit_extender_2
  or or_9 (or_9_out, and_1_out, BSA_t4_out);
  assign bit_extender_3_out = {{5{1'b0}}, PC_data_out};  // Bit_Extender bit_extender_3
  // Probe on DR_data_out
  Clock clock_1 (.out(clock_1_out));
  or or_10 (or_10_out, or_9_out, or_8_out);
  // Probe on bit_extender_3_out
  RAM #(.addrWidth(15), .dataWidth(20), .bus("separate")) ram_1 (
    .addr(AR_data_out), .din(multiplexer_1_out), .data(ram_1_data), .str(or_9_out), .sel(or_10_out),
    .clk(clock_1_out), .ld(or_8_out));  // open: clr
  // Probe on ac_1_out_5
  // Probe on ram_1_data
  Multiplexer #(.select(3), .width(20)) multiplexer_1 (
    .in1(bit_extender_2_out), .in2(bit_extender_3_out), .in3(DR_data_out), .in4(ac_1_out_5),
    .in5({IR_data_out_2[19], IR_data_out, IR_data_out_2[14:0]}), .in6(TR_data_out), .in7(ram_1_data),
    .out(multiplexer_1_out), .sel(priority_encoder_1_out), .en(1'b1));  // open: in0

  // Notes on the sheet:
  //   T
  //   T4
  //   STA
  //   BSA T5
  //   ISZ
  //   Indirect
  //   BSA T4
  //   STA
  //   Indirect MRI
  //   BUN
  //   BUN
  //   DR ma memoy load garna
  //   ISZ T6
  //   20 Bit Data Bus
  //   2
  //   3
  //   4
  //   5
  //   6
  //   7
  //   1
endmodule

module AC (
  input  [19:0] Bus,
  input  [19:0] D,
  input  [3:0] D_2,
  input  [15:0] Time_Input,
  output [19:0] out_5,
  output out_6
);

  wire alu_v2_1_bit_out, and_1_out, and_2_out, and_3_out, and_4_out, and_5_out, and_6_out, and_7_out,
       and_8_out, clock_1_out, decoder_1_out0, decoder_1_out1, decoder_1_out2, decoder_1_out3,
       decoder_1_out4, decoder_1_out5, decoder_1_out6, decoder_1_out7, or_1_out, or_2_out,
       priority_encoder_1_en_out;
  wire [3:0] priority_encoder_1_out;
  wire [19:0] alu_v2_1_out_5, multiplexer_1_out;

  Decoder #(.select(4)) decoder_1 (
    .out0(decoder_1_out0), .out1(decoder_1_out1), .out2(decoder_1_out2), .out3(decoder_1_out3),
    .out4(decoder_1_out4), .out5(decoder_1_out5), .out6(decoder_1_out6), .out7(decoder_1_out7), .sel(D_2));  // open: out8, out9, out10, out11, out12, out13, out14, out15, en
  and and_1 (and_1_out, Time_Input[5], decoder_1_out0);
  and and_2 (and_2_out, Time_Input[5], decoder_1_out1);
  and and_3 (and_3_out, Time_Input[5], decoder_1_out2);
  and and_4 (and_4_out, Time_Input[5], decoder_1_out3);
  and and_5 (and_5_out, Time_Input[5], decoder_1_out4);
  or or_1 (or_1_out, decoder_1_out0, decoder_1_out1, decoder_1_out2, decoder_1_out3, decoder_1_out4, decoder_1_out5, decoder_1_out6);
  and and_6 (and_6_out, Time_Input[5], decoder_1_out5);
  and and_7 (and_7_out, or_1_out, Time_Input[5]);
  // Probe on D
  and and_8 (and_8_out, Time_Input[5], decoder_1_out6);
  Multiplexer #(.width(20)) multiplexer_1 (.in0(Bus), .in1(D), .out(multiplexer_1_out), .sel(1'b1));  // open: en
  // Probe on multiplexer_1_out
  Priority_Encoder #(.select(4)) priority_encoder_1 (
    .in0(and_5_out), .in1(and_6_out), .in4(and_1_out), .in5(and_2_out), .in6(and_3_out), .in7(and_4_out),
    .in12(and_8_out), .out(priority_encoder_1_out), .en_out(priority_encoder_1_en_out));  // open: in2, in3, in8, in9, in10, in11, in13, in14, in15, gs, en_in
  // Probe on priority_encoder_1_out
  Clock clock_1 (.out(clock_1_out));
  ALU_V2 alu_v2_1 (
    .A(out_5), .in_1(priority_encoder_1_out), .B(multiplexer_1_out), .Bit_In(1'b0),
    .Bit_Out(alu_v2_1_bit_out), .out_5(alu_v2_1_out_5));
  // Probe on alu_v2_1_out_5
  D_Flip_Flop E (
    .clk(clock_1_out), .D(alu_v2_1_bit_out), .Q(out_6), .preset(1'b0), .en(1'b1), .reset(1'b0));  // open: Qn
  buf or_2 (or_2_out, and_7_out);  // OR_Gate
  _20Bit_Custom_Register u_20bit_custom_register_1 (
    .Data_In(alu_v2_1_out_5), .Data_Out(out_5), .CLR(1'b0), .INC(1'b0), .LDA(or_2_out));
endmodule

module BUS_AND_REGISTERS (
  input  in_1
);

  wire ac_1_out_6, and_1_out, and_2_out, and_3_out, button_1_out, button_2_out, button_3_out, button_4_out,
       button_5_out, button_6_out, button_7_out, button_8_out, button_9_out, clock_1_out, decoder_1_out0,
       decoder_1_out1, decoder_1_out2, decoder_1_out3, decoder_1_out4, decoder_1_out5, decoder_1_out6,
       decoder_1_out7, decoder_1_out8, decoder_1_out9, decoder_1_out10, decoder_1_out11, decoder_1_out12,
       decoder_1_out13, decoder_1_out14, decoder_1_out15, DR_ko_lagi_out, nor_1_out, or_1_out, or_2_out,
       or_3_out, or_4_out, or_5_out, or_6_out, or_7_out;
  wire [2:0] priority_encoder_1_out;
  wire [14:0] AR_data_out, bit_extender_1_out, PC_data_out;
  wire [15:0] sc_1_t;
  wire [19:0] ac_1_out_5, bit_extender_2_out, bit_extender_3_out, DR_data_out, IR_data_out,
       multiplexer_1_out, ram_1_data, TR_data_out;

  SC sc_1 (.T(sc_1_t));  // open: D_opcode_data_used_to_reset_clock_pulse, I, AR
  nor nor_1 (nor_1_out, sc_1_t[0], sc_1_t[1]);
  Decoder #(.select(4)) decoder_1 (
    .out0(decoder_1_out0), .out1(decoder_1_out1), .out2(decoder_1_out2), .out3(decoder_1_out3),
    .out4(decoder_1_out4), .out5(decoder_1_out5), .out6(decoder_1_out6), .out7(decoder_1_out7),
    .out8(decoder_1_out8), .out9(decoder_1_out9), .out10(decoder_1_out10), .out11(decoder_1_out11),
    .out12(decoder_1_out12), .out13(decoder_1_out13), .out14(decoder_1_out14), .out15(decoder_1_out15),
    .sel(IR_data_out[18:15]), .en(nor_1_out));
  or or_1 (or_1_out, and_1_out, in_1);
  buf or_2 (or_2_out, and_2_out);  // OR_Gate
  and and_1 (and_1_out, sc_1_t[5], decoder_1_out8);
  buf or_3 (or_3_out, sc_1_t[0]);  // OR_Gate
  or or_4 (or_4_out, sc_1_t[1], and_3_out);
  buf or_5 (or_5_out, sc_1_t[2]);  // OR_Gate
  and and_2 (and_2_out, sc_1_t[4], decoder_1_out8);
  or DR_ko_lagi (DR_ko_lagi_out, decoder_1_out0, decoder_1_out1, decoder_1_out2, decoder_1_out3, decoder_1_out4, decoder_1_out5, decoder_1_out6, decoder_1_out10, decoder_1_out11);
  or or_6 (or_6_out, sc_1_t[2], sc_1_t[0]);
  and and_3 (and_3_out, sc_1_t[4], DR_ko_lagi_out);
  Priority_Encoder priority_encoder_1 (
    .in1(or_2_out), .in2(or_3_out), .in5(or_5_out), .in7(or_4_out), .out(priority_encoder_1_out), .en_in(1'b1));  // open: in0, in3, in4, in6, gs, en_out
  or or_7 (or_7_out, and_3_out, sc_1_t[1]);
  // Probe on multiplexer_1_out
  Bit_Extender #(.in_width(20), .out_width(15)) bit_extender_1 (.in(multiplexer_1_out), .out(bit_extender_1_out));
  // Probe on bit_extender_1_out
  Button button_1 (.out(button_1_out));
  // Probe on priority_encoder_1_out
  Button button_2 (.out(button_2_out));
  _15Bit_Custom_Register AR (
    .Data_In(bit_extender_1_out), .Data_Out(AR_data_out), .CLR(button_2_out), .INC(button_1_out),
    .LDA(or_6_out));
  Button button_3 (.out(button_3_out));
  Button button_4 (.out(button_4_out));
  Button button_5 (.out(button_5_out));
  Button button_6 (.out(button_6_out));
  _20Bit_Custom_Register IR (
    .Data_In(multiplexer_1_out), .Data_Out(IR_data_out), .CLR(button_7_out), .INC(button_3_out),
    .LDA(sc_1_t[1]));
  Button button_7 (.out(button_7_out));
  Button button_8 (.out(button_8_out));
  _15Bit_Custom_Register PC (
    .Data_In(bit_extender_1_out), .Data_Out(PC_data_out), .CLR(button_4_out), .INC(sc_1_t[1]), .LDA(and_2_out));
  _20Bit_Custom_Register DR (
    .Data_In(multiplexer_1_out), .Data_Out(DR_data_out), .CLR(button_6_out), .INC(button_5_out),
    .LDA(and_3_out));
  // Probe on IR_data_out
  _20Bit_Custom_Register TR (
    .Data_In(multiplexer_1_out), .Data_Out(TR_data_out), .CLR(button_9_out), .INC(button_8_out));  // open: LDA
  Button button_9 (.out(button_9_out));
  // Probe on AR_data_out
  // Probe on PC_data_out
  AC ac_1 (
    .D(DR_data_out), .Time_Input(sc_1_t), .D_2(IR_data_out[18:15]), .out_5(ac_1_out_5), .out_6(ac_1_out_6));  // open: Bus
  assign bit_extender_2_out = {{5{1'b0}}, AR_data_out};  // Bit_Extender bit_extender_2
  assign bit_extender_3_out = {{5{1'b0}}, PC_data_out};  // Bit_Extender bit_extender_3
  // Probe on DR_data_out
  Clock clock_1 (.out(clock_1_out));
  // Probe on bit_extender_3_out
  RAM #(.addrWidth(15), .dataWidth(20), .bus("separate")) ram_1 (
    .addr(AR_data_out), .data(ram_1_data), .str(1'b0), .sel(or_7_out), .clk(clock_1_out), .ld(or_7_out));  // open: din, clr
  // Probe on ram_1_data
  Multiplexer #(.select(3), .width(20)) multiplexer_1 (
    .in1(bit_extender_2_out), .in2(bit_extender_3_out), .in3(DR_data_out), .in4(ac_1_out_5),
    .in5(IR_data_out), .in6(TR_data_out), .in7(ram_1_data), .out(multiplexer_1_out),
    .sel(priority_encoder_1_out), .en(1'b1));  // open: in0

  // Notes on the sheet:
  //   T
  //   T4
  //   BUN
  //   BUN
  //   BUN
  //   DR ma memoy load garna
  //   20 Bit Data Bus
  //   2
  //   3
  //   4
  //   5
  //   6
  //   7
  //   1
endmodule
